// Logisim project OC.circ as structural Verilog: 9 circuits, main circuit somador8bits
module main (
  input  in_1,
  input  [7:0] in_2,
  input  [7:0] in_3,
  input  in_4,
  input  in_5,
  input  in_6,
  input  [7:0] in_7,
  output [7:0] out_8,
  output out_9,
  output out_10,
  output [7:0] out_11
);

  Memoria1Bit memoria1bit_1 (.S(in_5), .I(in_4), .Q(out_10));
  Memoria8Bits memoria8bits_1 (.in_2(in_7), .in_1(in_6), .out_3(out_11));
  Registrador registrador_1 ();  // open: I, S, E, O
  somador8bits somador8bits_1 (.B(in_3), .A(in_2), .in_2(in_1), .S(out_8), .out_4(out_9));
endmodule

module somador1bit (
  input  Cin,
  input  A,
  input  B,
  output S,
  output Cout
);

  wire and_1_out, and_2_out, xor_1_out;

  and and_1 (and_1_out, A, B);
  xor xor_1 (xor_1_out, A, B);
  or or_1 (Cout, and_1_out, and_2_out);
  and and_2 (and_2_out, xor_1_out, Cin);
  xor xor_2 (S, Cin, xor_1_out);
endmodule

module somador8bits (
  input  [7:0] A,
  input  in_2,
  input  [7:0] B,
  output out_4,
  output [7:0] S
);

  wire somador1bit_1_cout, somador1bit_3_cout, somador1bit_4_cout, somador1bit_5_cout, somador1bit_6_cout,
       somador1bit_7_cout;

  somador1bit somador1bit_1 (.A(A[0]), .B(B[0]), .Cin(in_2), .Cout(somador1bit_1_cout), .S(S[0]));
  somador1bit somador1bit_2 (.A(A[1]), .B(B[1]), .Cin(somador1bit_1_cout), .Cout(B[2]), .S(S[1]));
  somador1bit somador1bit_3 (.A(A[2]), .B(B[2]), .Cin(B[2]), .Cout(somador1bit_3_cout), .S(S[2]));
  somador1bit somador1bit_4 (.A(A[3]), .B(B[3]), .Cin(somador1bit_3_cout), .Cout(somador1bit_4_cout), .S(S[3]));
  somador1bit somador1bit_5 (.A(A[4]), .B(B[4]), .Cin(somador1bit_4_cout), .Cout(somador1bit_5_cout), .S(S[4]));
  somador1bit somador1bit_6 (.A(A[5]), .B(B[5]), .Cin(somador1bit_5_cout), .Cout(somador1bit_6_cout), .S(S[5]));
  somador1bit somador1bit_7 (.A(A[6]), .B(B[6]), .Cin(somador1bit_6_cout), .Cout(somador1bit_7_cout), .S(S[6]));
  somador1bit somador1bit_8 (.A(A[7]), .B(B[7]), .Cin(somador1bit_7_cout), .Cout(out_4), .S(S[7]));
endmodule

module Memoria1Bit (
  input  I,
  input  S,
  output Q
);

  wire nand_1_out, nand_2_out, nand_4_out;

  nand nand_1 (nand_1_out, I, S);
  nand nand_2 (nand_2_out, nand_1_out, S);
  nand nand_3 (Q, nand_1_out, nand_4_out);
  nand nand_4 (nand_4_out, Q, nand_2_out);

  // Notes on the sheet:
  //   Input | Set | Output
  //   0   |  0  |  x
  //   1   |  0  |  x
  //   0   |  1  |  0
  //   1   |  1  |  1
  //   (armazenado)
  //   (armazenado)
endmodule

module Memoria8Bits (
  input  in_1,
  input  [7:0] in_2,
  output [7:0] out_3
);

  Memoria1Bit memoria1bit_1 (.S(in_1), .I(in_2[0]), .Q(out_3[0]));
  Memoria1Bit memoria1bit_2 (.S(in_1), .I(in_2[1]), .Q(out_3[1]));
  Memoria1Bit memoria1bit_3 (.S(in_1), .I(in_2[2]), .Q(out_3[2]));
  Memoria1Bit memoria1bit_4 (.S(in_1), .I(in_2[3]), .Q(out_3[3]));
  Memoria1Bit memoria1bit_5 (.S(in_1), .I(in_2[4]), .Q(out_3[4]));
  Memoria1Bit memoria1bit_6 (.S(in_1), .I(in_2[5]), .Q(out_3[5]));
  Memoria1Bit memoria1bit_7 (.S(in_1), .I(in_2[6]), .Q(out_3[6]));
  Memoria1Bit memoria1bit_8 (.S(in_1), .I(in_2[7]), .Q(out_3[7]));
endmodule

module Registrador (
  input  S,
  input  [7:0] I,
  input  E,
  output [7:0] O
);

  wire [7:0] memoria8bits_1_out_3;

  Memoria8Bits memoria8bits_1 (.in_2(I), .in_1(S), .out_3(memoria8bits_1_out_3));
  and and_1 (O[0], memoria8bits_1_out_3[0], E);
  and and_2 (O[1], memoria8bits_1_out_3[1], E);
  and and_3 (O[2], memoria8bits_1_out_3[2], E);
  and and_4 (O[3], memoria8bits_1_out_3[3], E);
  and and_5 (O[4], memoria8bits_1_out_3[4], E);
  and and_6 (O[5], memoria8bits_1_out_3[5], E);
  and and_7 (O[6], memoria8bits_1_out_3[6], E);
  and and_8 (O[7], memoria8bits_1_out_3[7], E);
endmodule

module Memoria1byte (
  input  Set,
  input  [7:0] Inp,
  output out_3,
  output out_4,
  output out_5,
  output out_6,
  output out_7,
  output out_8,
  output out_9,
  output out_10
);

  Memoria1Bit memoria1bit_1 (.S(Set), .I(Inp[0]), .Q(out_3));
  Memoria1Bit memoria1bit_2 (.S(Set), .I(Inp[1]), .Q(out_4));
  Memoria1Bit memoria1bit_3 (.S(Set), .I(Inp[2]), .Q(out_5));
  Memoria1Bit memoria1bit_4 (.S(Set), .I(Inp[3]), .Q(out_6));
  Memoria1Bit memoria1bit_5 (.S(Set), .I(Inp[4]), .Q(out_7));
  Memoria1Bit memoria1bit_6 (.S(Set), .I(Inp[5]), .Q(out_8));
  Memoria1Bit memoria1bit_7 (.S(Set), .I(Inp[6]), .Q(out_9));
  Memoria1Bit memoria1bit_8 (.S(Set), .I(Inp[7]), .Q(out_10));
endmodule

module Controll_buffer (
  input  [7:0] in_1,
  input  in_2,
  input  in_3,
  input  in_4,
  input  in_5,
  input  [7:0] in_6,
  input  in_7,
  input  in_8,
  input  in_9,
  input  [7:0] in_10,
  output [7:0] out_11
);

  wire [7:0] register_1_q, register_2_q;

  Register register_1 (.D(in_1), .Q(register_1_q), .clk(in_5));  // open: en, clr
  assign out_11 = in_3 ? register_1_q : 8'bz;  // Controlled_Buffer controlled_buffer_1
  RAM #(.databus("bidir")) ram_1 (.addr(in_6), .we(in_7), .oe(in_8), .clk(in_9), .data(in_10));
  Register register_2 (.D(in_1), .Q(register_2_q), .clk(in_4));  // open: en, clr
  assign out_11 = in_2 ? register_2_q : 8'bz;  // Controlled_Buffer controlled_buffer_2
endmodule

module MEM_RAM (
  input  [7:0] Dado,
  input  in_2,
  input  [7:0] Endereco,
  input  in_4,
  input  in_5,
  output [7:0] out_6
);

  wire and_1_out, and_2_out, and_3_out, and_4_out, and_5_out, and_6_out, and_7_out, and_8_out, and_9_out,
       decoder_1_out0, decoder_1_out1, decoder_1_out2, decoder_2_out0, undriven_3, undriven_4, undriven_5,
       undriven_6, undriven_7, undriven_8;
  wire [7:0] controlled_buffer_7_out, controlled_buffer_8_out, register_1_q, register_2_q, register_3_q,
       register_4_q, register_5_q, register_6_q, register_7_q, undriven, undriven_2;

  Decoder #(.select(4)) decoder_1 (
    .out0(decoder_1_out0), .out1(decoder_1_out1), .out2(decoder_1_out2), .sel(Endereco[3:0]));  // open: out3, out4, out5, out6, out7, out8, out9, out10, out11, out12, out13, out14, out15, en
  Decoder #(.select(4)) decoder_2 (
    .out0(decoder_2_out0), .sel(Endereco[7:4]));  // open: out1, out2, out3, out4, out5, out6, out7, out8, out9, out10, out11, out12, out13, out14, out15, en
  Register register_1 (.D(Dado), .Q(register_1_q), .clk(in_2));  // open: en, clr
  and and_1 (and_1_out, decoder_1_out0, decoder_2_out0);
  Register register_2 (.D(undriven), .Q(register_2_q), .clk(in_4));  // open: en, clr
  and and_2 (and_2_out, undriven_4, decoder_2_out0);
  Register register_3 (.D(undriven_2), .Q(register_3_q), .clk(in_5));  // open: en, clr
  and and_3 (and_3_out, undriven_3, decoder_2_out0);
  assign register_2_q = and_1_out ? register_1_q : 8'bz;  // Controlled_Buffer controlled_buffer_1
  assign register_3_q = and_2_out ? register_2_q : 8'bz;  // Controlled_Buffer controlled_buffer_2
  assign out_6 = and_3_out ? register_3_q : 8'bz;  // Controlled_Buffer controlled_buffer_3
  Register register_4 (.D(Dado), .Q(register_4_q));  // open: en, clk, clr
  and and_4 (and_4_out, decoder_1_out1, decoder_2_out0);
  Register register_5 (.D(undriven), .Q(register_5_q));  // open: en, clk, clr
  and and_5 (and_5_out, undriven_5, decoder_2_out0);
  Register register_6 (.D(undriven_2), .Q(register_6_q));  // open: en, clk, clr
  and and_6 (and_6_out, undriven_6, decoder_2_out0);
  assign register_5_q = and_4_out ? register_4_q : 8'bz;  // Controlled_Buffer controlled_buffer_4
  assign register_6_q = and_5_out ? register_5_q : 8'bz;  // Controlled_Buffer controlled_buffer_5
  assign out_6 = and_6_out ? register_6_q : 8'bz;  // Controlled_Buffer controlled_buffer_6
  and and_7 (and_7_out, decoder_1_out2, decoder_2_out0);
  and and_8 (and_8_out, undriven_7, decoder_2_out0);
  and and_9 (and_9_out, undriven_8, decoder_2_out0);
  Register register_7 (.D(Dado), .Q(register_7_q));  // open: en, clk, clr
  assign controlled_buffer_7_out = and_7_out ? register_7_q : 8'bz;  // Controlled_Buffer controlled_buffer_7
  Register register_8 (.D(undriven), .Q(controlled_buffer_7_out));  // open: en, clk, clr
  assign controlled_buffer_8_out = and_8_out ? controlled_buffer_7_out : 8'bz;  // Controlled_Buffer controlled_buffer_8
  Register register_9 (.D(undriven_2), .Q(controlled_buffer_8_out));  // open: en, clk, clr
  assign out_6 = and_9_out ? controlled_buffer_8_out : 8'bz;  // Controlled_Buffer controlled_buffer_9
endmodule
